# Fritzing sketch Water Cannon Sketch (saved by Fritzing 0.8.0b)
breadboards: 2

parts:
  LED1 = LED - 5mm [color="Red (633nm)" package="5 mm [THT]"]
  Part1 = Arduino Uno (Rev3)
  R1 = Resistor [tolerance=±5% resistance=3.3k package=THT]
  D1 = Rectifier Diode [part_number=1N4001 package="300 mil [THT]"]
  Q1 = NPN-Transistor [part_number=2N3904 package="TO92 [THT]"]
  M1 = DC Motor
  R2 = Resistor [tolerance=±5% resistance=220 package=THT]
  VCC1 = 4 x AAA Battery Mount
  J1 = Basic Servo
  R3 = Resistor [tolerance=±5% resistance=220 package=THT]

nets (from the breadboard view):
  GND: LED1.cathode, Part1.GND, Q1.C, VCC1.-, J1.gnd
  N1: LED1.anode, R2.Pin_1
  N2: Part1.D9_PWM, R3.Pin_1
  N3: Part1.D3_PWM, R1.Pin_0
  N4: Part1.D5_PWM, R2.Pin_0
  3V3: Part1.3V3, J1.vcc
  N5: R1.Pin_1, Q1.B
  N6: D1.cathode, M1.pin_2, VCC1.+
  N7: D1.anode, Q1.E, M1.pin_1
  N8: J1.pulse, R3.Pin_0

notes:
  The resistor on pin 3 is to prevent accidental short circuit.
  The DC motor represents the water pump.
  The servo controls the water hose/pipe delivering water through the water pump.
