# Fritzing sketch game_of_life (saved by Fritzing 0.8.0b)
breadboards: 1

parts:
  Nokia_5110_LCD_Module2 = Nokia5110LCDModule
  Part1 = Arduino Uno (Rev3)
  R2 = Resistor [tolerance=±5% resistance=3.6k package=THT]
  R3 = Resistor [tolerance=±5% resistance=3.6k package=THT]
  R5 = Resistor [tolerance=±5% resistance=3.6k package=THT]
  R6 = Resistor [tolerance=±5% resistance=220 package=THT]  # not connected
  R7 = Resistor [tolerance=±5% resistance=3.6k package=THT]
  R8 = Resistor [tolerance=±5% resistance=3.6k package=THT]
  R9 = Resistor [tolerance=±5% resistance=2.4k package=THT]
  R10 = Resistor [tolerance=±5% resistance=2.4k package=THT]
  R11 = Resistor [tolerance=±5% resistance=2.4k package=THT]
  R12 = Resistor [tolerance=±5% resistance=2.4k package=THT]
  R13 = Resistor [tolerance=±5% resistance=2.4k package=THT]
  R14 = Rotary Potentiometer (Small)

nets:
  N1: Nokia_5110_LCD_Module2.Vcc, R2.Pin_1, R9.Pin_0
  N2: Nokia_5110_LCD_Module2.Grnd, R3.Pin_1, R10.Pin_0
  N3: Nokia_5110_LCD_Module2.SCE, R7.Pin_1, R11.Pin_0
  N4: Nokia_5110_LCD_Module2.RST, R5.Pin_0, R12.Pin_0
  N5: Nokia_5110_LCD_Module2.D/C, R8.Pin_0, R13.Pin_0
  N6: Nokia_5110_LCD_Module2.SCLK, Part1.D3_PWM
  N7: Nokia_5110_LCD_Module2.LED, Part1.GND, R2.Pin_0, R3.Pin_0, R5.Pin_1, R7.Pin_0, R8.Pin_1, R14.leg1
  N8: Part1.A1, R14.wiper
  N9: Part1.ICSP_SCK, Part1.D13/SCK, R13.Pin_1
  N10: Part1.ICSP_MOSI, Part1.D11_PWM/MOSI, R12.Pin_1
  N11: Part1.D5_PWM, R11.Pin_1
  N12: Part1.D6_PWM, R10.Pin_1
  N13: Part1.D7, R9.Pin_1
  N14: Part1.3V3, R14.leg2

custom parts:
  : Nokia 5110 LCD with 8 pin. It's a 45mm*45mm module part. Description: The Nokia 5110 is a basic graphic LCD screen for lots of applications. It was originally intended for as a cell phone screen. This one is mounted on an easy to solder PCB. It uses the PCD8544 controller. The PCD8544 is a low power CMOS LCD controller/driver, designed to drive a graphic display of 48 rows and 84 columns. All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
