# Fritzing sketch Water Pump Sketch Low Power (saved by Fritzing 0.8.0b)
breadboards: 1

parts:
  Part1 = Arduino Pro Mini v13
  VCC1 = 4 x AAA Battery Mount
  Q1 = NPN-Transistor [part_number=S9013 package="TO92 [THT]"]
  R1 = Resistor [tolerance=±5% resistance=1.0k package=THT]
  D1 = Rectifier Diode [part_number=1N4001 package="300 mil [THT]"]
  M1 = DC Motor
  VCC2 = 4 x AAA Battery Mount

nets:
  N1: Part1.RAW, VCC1.+
  N2: Part1.GND, VCC1.-, Q1.E, VCC2.-
  N3: Part1.D3_PWM, R1.Pin_0
  N4: Q1.B, R1.Pin_1
  N5: Q1.C, D1.anode, M1.pin_1
  N6: D1.cathode, M1.pin_2, VCC2.+

notes:
  4.5V to power the board
  6V to power the water pump
  The water pump
